# Fritzing sketch SidBoard1 (saved by Fritzing 0.8.5b)
circuit board: 7.62cm x 10.16cm
breadboards: 1

parts:
  C1 = Capacitor [package=cap-pth-small-kit]
  C2 = Capacitor [part_number=.1u package=cap-pth-small-kit]
  C3 = Capacitor [part_number=1u package=cap-pth-small-kit]
  C4 = Capacitor [part_number=.1u package=cap-pth-small-kit]
  C5 = Capacitor [part_number=1u package=cap-pth-small-kit]
  U2 = mystery part, 48 pins [chip_label=CMOD]
  U3 = mystery part, 28 pins [chip_label=?]
  U1 = mystery part, 28 pins [chip_label=SID]

nets:
  audio out: C1.1
  N1: C1.2, U1.pin27
  5V: C2.1, C3.1, U1.pin25
  GND: C2.2, C3.2, C4.2, C5.2, U2.pin25, U1.pin7, U1.pin14
  9V: C4.1, C5.1, U1.pin28
  N2: U2.pin1, U1.pin5
  N3: U2.pin2, U1.pin6
  N4: U2.pin3, U1.pin8
  N5: U2.pin4, U1.pin9
  N6: U2.pin5, U1.pin10
  N7: U2.pin6, U1.pin11
  N8: U2.pin7, U1.pin12
  N9: U2.pin8, U1.pin13
  N10: U2.pin9, U3.pin22
  N11: U2.pin10, U3.pin21
  N12: U2.pin11, U3.pin20
  N13: U2.pin12, U3.pin19
  N14: U2.pin13, U3.pin18
  N15: U2.pin14, U3.pin17
  N16: U2.pin15, U3.pin16
  N17: U2.pin16, U3.pin15
  N18: U2.pin17, U3.pin5
  N19: U2.pin18, U3.pin6
  N20: U2.pin19, U3.pin8
  N21: U2.pin20, U3.pin13
  N22: U2.pin21, U3.pin12
  N23: U2.pin22, U3.pin11
  N24: U2.pin23, U3.pin10
  6V: U2.pin24
  N25: U2.pin26, U3.pin9
  N26: U2.pin41, U1.pin15
  N27: U2.pin42, U1.pin16
  N28: U2.pin43, U1.pin17
  N29: U2.pin44, U1.pin18
  N30: U2.pin45, U1.pin19
  N31: U2.pin46, U1.pin20
  N32: U2.pin47, U1.pin21
  N33: U2.pin48, U1.pin22

notes:
  APHID.Y0 (c) TweakoZ
