# Fritzing sketch SidBoardV2 (saved by Fritzing 0.9.1b)
circuit board: 7.62cm x 10.16cm
breadboards: 1

parts:
  U1 = mystery part, 28 pins [chip_label=SID]
  U4 = mystery part, 14 pins [chip_label=?]
  U2 = mystery part, 48 pins [chip_label=CMOD]

nets:
  N1: U1.pin5, U2.pin5
  N2: U1.pin6, U2.pin6
  GND: U1.pin7, U1.pin14, U2.pin25
  N3: U1.pin8, U2.pin7
  N4: U1.pin9, U2.pin43
  N5: U1.pin10, U2.pin44
  N6: U1.pin11, U2.pin45
  N7: U1.pin12, U2.pin46
  N8: U1.pin13, U2.pin47
  N9: U1.pin15, U2.pin42
  N10: U1.pin16, U2.pin41
  N11: U1.pin17, U2.pin40
  N12: U1.pin18, U2.pin39
  N13: U1.pin19, U2.pin38
  N14: U1.pin20, U2.pin37
  N15: U1.pin21, U2.pin36
  N16: U1.pin22, U2.pin35
  N17: U1.pin27, U4.pin3
  N18: U4.pin1, U4.pin2
  6V: U2.pin24
